# Fritzing sketch rfid_cloner (saved by Fritzing 0.9.6b)

parts:
  Part1 = Arduino Leonardo (Rev3b)
  Part2 = RFID-RC522-v2

nets:
  3V3: Part1.3V3, Part2.3.3V
  N1: Part1.D9_PWM/A9, Part2.RST
  N2: Part1.D10_PWM/A10, Part2.SDA
  N3: Part1.D11_PWM, Part2.MOSI
  N4: Part1.D12/A11, Part2.MISO
  N5: Part1.D13_PWM, Part2.SCK
  GND: Part1.GND, Part2.GND

custom parts:
  RFID-RC522-v2: A simple China made RFID-RC522 Reader; do check the pin labels, as this is a MFRC522 based clone.
